# Fritzing sketch Matrix 8x8 Game Breadboards (saved by Fritzing 0.9.3b)
perfboards: 3

parts:
  J1 = Piezo Speaker  # not connected
  RCWL-0516_Microwave_Radar_Motion_Sensor1 = RCWL-0516 Microwave Radar Motion Sensor Module  # not connected
  Nano1 = Arduino Nano v2.3  # not connected
  JP1 = Header 8 [package=1x08_smd]
  JP2 = Header 8 [package=1x08_smd]
  JP3 = Header 8 [package=1x08_smd]  # not connected
  JP4 = Header 8 [package=1x08_smd]  # not connected
  JP5 = Header 8 [package=1x08_smd]
  JP6 = Header 8 [package=1x08_smd]
  R20 = Resistor [tolerance=±5% resistance=1M package="2512 [SMD]"]  # not connected
  J2 = Piezo Speaker  # not connected
  R21 = Resistor [tolerance=±5% resistance=1k package=THT]
  R22 = Resistor [tolerance=±5% resistance=1k package=THT]
  R23 = Resistor [tolerance=±5% resistance=1k package=THT]
  R25 = Resistor [tolerance=±5% resistance=1k package=THT]
  R26 = Resistor [tolerance=±5% resistance=1k package=THT]
  R27 = Resistor [tolerance=±5% resistance=1k package=THT]
  R29 = Resistor [tolerance=±5% resistance=1k package=THT]
  R30 = Resistor [tolerance=±5% resistance=1k package=THT]
  JP7 = Header 8 [package=1x08_smd]
  JP8 = Header 8 [package=1x08_smd]  # not connected
  JP9 = Header 8 [package=1x08_smd]
  JP10 = Header 8 [package=1x08_smd]
  R31 = Resistor [tolerance=±5% resistance=1k package=THT]
  R32 = Resistor [tolerance=±5% resistance=1k package=THT]
  R33 = Resistor [tolerance=±5% resistance=1k package=THT]
  R34 = Resistor [tolerance=±5% resistance=1k package=THT]
  R35 = Resistor [tolerance=±5% resistance=1k package=THT]
  R36 = Resistor [tolerance=±5% resistance=1k package=THT]
  R38 = Resistor [tolerance=±5% resistance=1k package=THT]
  R37 = Resistor [tolerance=±5% resistance=1k package=THT]

nets:
  N1: JP1.1, R26.Pin_1
  N2: JP1.2, R25.Pin_1
  N3: JP1.3, JP5.6
  N4: JP1.4, R23.Pin_1
  N5: JP1.5, JP5.4
  N6: JP1.6, JP5.3
  N7: JP1.7, R22.Pin_1
  N8: JP1.8, R21.Pin_1
  N9: JP2.1, R29.Pin_0
  N10: JP2.2, JP6.7
  N11: JP2.3, JP6.6
  N12: JP2.4, R30.Pin_0
  N13: JP2.5, JP6.4
  N14: JP2.6, R27.Pin_0
  N15: JP2.7, JP6.2
  N16: JP2.8, JP6.1
  N17: JP6.3, R27.Pin_1
  N18: JP6.5, R30.Pin_1
  N19: JP6.8, R29.Pin_1
  N20: JP7.1, JP9.8
  N21: JP7.2, JP9.7
  N22: JP7.4, JP9.5
  N23: JP7.6, JP9.3
  N24: JP7.7, JP9.2
  N25: JP9.1, R36.Pin_0
  N26: JP9.4, R37.Pin_0
  N27: JP9.6, R38.Pin_0
  N28: JP10.1, R33.Pin_1
  N29: JP10.2, R35.Pin_1
  N30: JP10.4, R34.Pin_1
  N31: JP10.7, R32.Pin_1
  N32: JP10.8, R31.Pin_1

custom parts:
  RCWL-0516 Microwave Radar Motion Sensor Module: The RCWL-0516 is a microwave radar motion sensor module. Input voltage is 4V to 28V. The 3V3 pin is a power output.
